# Fritzing sketch Lochraster (saved by Fritzing 0.9.2b)
perfboards: 2

parts:
  Bauteil1 = Arduino Nano (Rev3.0)
  J1 = female pin header, 1 pin [form="♀ (female)"]
  J2 = female pin header, 1 pin [form="♀ (female)"]
  J3 = female pin header, 1 pin [form="♀ (female)"]
  J4 = female pin header, 1 pin [form="♀ (female)"]
  J5 = Power Jack [package=power_jack_pth_lock]
  J6 = female pin header, 9 pins [form="♀ (female)"]
  J7 = female pin header, 5 pins [form="♀ (female)"]
  J8 = female pin header, 4 pins [form="♀ (female)"]
  J9 = female pin header, 4 pins [form="♀ (female)"]
  Photo1 = Photocell (LDR) [package=THT]  # not connected
  S1 = Pushbutton [package="[THT]"]
  S2 = Pushbutton [package="[THT]"]
  S3 = Pushbutton [package="[THT]"]
  S4 = Pushbutton [package="[THT]"]
  U2 = mystery part, 4 pins [chip_label=Piezo]  # not connected
  ZS-042_RTC1 = ZS-042 RTC Module  # not connected
  R1 = Rotary Potentiometer (Large) [maximum_resistance=100kΩ package=THT]  # not connected

nets:
  N1: Bauteil1.GND, J4.pin1, J8.pin1, J8.pin2
  N2: Bauteil1.D2, J6.pin6
  N3: Bauteil1.D3, J6.pin5
  N4: Bauteil1.D4, J6.pin4
  N5: Bauteil1.D5, J6.pin3
  N6: Bauteil1.D6, J6.pin2
  N7: Bauteil1.D7, J7.pin1
  N8: Bauteil1.D8, J8.pin3
  N9: Bauteil1.D9, J9.pin3
  N10: Bauteil1.D10, J9.pin4
  N11: Bauteil1.5V, J2.pin1
  N12: Bauteil1.A7, J6.pin9
  N13: Bauteil1.A6, J6.pin7
  N14: J1.pin1, J5.GND
  N15: J3.pin1, J5.PWR
  N16: S1.Pin_1, S1.Pin_2
  N17: S1.Pin_3, S1.Pin_4
  N18: S2.Pin_1, S2.Pin_2
  N19: S2.Pin_3, S2.Pin_4
  N20: S3.Pin_1, S3.Pin_2
  N21: S3.Pin_3, S3.Pin_4
  N22: S4.Pin_1, S4.Pin_2
  N23: S4.Pin_3, S4.Pin_4

notes:
  Gespiegelt aufgebaut
  o+ o-
  i+ i-
