# Fritzing sketch Wecker (saved by Fritzing 0.9.2b)
breadboards: 1

parts:
  Bauteil1 = Arduino Mega 2560 (Rev3)
  R1 = Resistor [tolerance=±5% resistance=10k package=THT]
  LED1 = LED - 5mm [color="Red (633nm)" package="5 mm [THT]"]
  S2 = Square Pushbutton
  S3 = Square Pushbutton
  R2 = Resistor [tolerance=±5% resistance=10k package=THT]
  R3 = Resistor [tolerance=±5% resistance=220 package=THT]

nets:
  N1: Bauteil1.GND, R1.Pin_1, R2.Pin_1, R3.Pin_1
  N2: Bauteil1.D2_PWM, R1.Pin_0, S2.leg1
  N3: Bauteil1.D3_PWM, LED1.cathode
  N4: Bauteil1.D42, S3.leg1, R2.Pin_0
  N5: LED1.anode, R3.Pin_0

// code stored in the sketch: Wecken_T1.ino
int klingel =3;
int aus=2;
int kick=42;

//Laufzeitvariablen
bool wecken=0;
bool blinken=0;




void setup() {
pinMode(klingel,OUTPUT);
pinMode(aus,INPUT);
pinMode(kick,INPUT);
}

void loop() {  
if (digitalRead(kick)==HIGH){
  wecken=1;
}
if (digitalRead(aus)==HIGH){
  wecken=0;
}
if (wecken){
  if (blinken) {
    digitalWrite(klingel,HIGH);
  }else{
    digitalWrite(klingel,LOW);    
  }
  blinken=!blinken;
}else{
  digitalWrite(klingel,LOW); 
}
delay(500);
}
